# Fritzing sketch wiring diagram (saved by Fritzing 0.9.3b)

parts:
  L2 = Solenoid
  U2 = RELAY [package=relay-jzc]
  U3 = RELAY [package=relay-jzc]
  L1 = Solenoid
  L3 = Solenoid
  U1 = RELAY [package=relay-jzc]
  U4 = ESP32S-HiLetgo [part_number=ESP32S-HiLetgo]
  Mod1 = ESP32 - CAM
  U5 = RELAY [package=relay-jzc]
  U6 = RELAY [package=relay-jzc]
  U7 = RELAY [package=relay-jzc]
  L4 = Solenoid
  L5 = Solenoid
  L6 = Solenoid

nets:
  N1: L2.pin1, L1.pin1, L3.pin1
  N2: L2.pin2, U2.MAIN
  N3: U2.COIL2, U4.GPIO23
  N4: U2.NC, U3.NC, U1.NC
  N5: U2.NO, U3.NO, U1.NO
  N6: U3.COIL2, U4.GPIO32
  N7: U3.MAIN, L3.pin2
  N8: L1.pin2, U1.MAIN
  N9: U1.COIL2, U4.GPIO33
  N10: U4.GPIO19, Mod1.VOR
  N11: U4.GPIO22, Mod1.VOT
  N12: Mod1.GND, Mod1.IO12, U6.COIL2
  N13: Mod1.IO13, U7.COIL2
  N14: Mod1.IO15, U5.COIL2
  N15: U5.NC, U6.NC, U7.NC
  N16: U5.NO, U6.NO, U7.NO
  N17: U5.MAIN, L6.pin2
  N18: U6.MAIN, L5.pin2
  N19: U7.MAIN, L4.pin2

notes:
  VCC
  GND

custom parts:
  ESP32S-HiLetgo: HiLetgo ESP-WROOM-32 ESP32 ESP-32S Development Board 2.4GHz Dual-Mode WiFi + Bluetooth Dual Cores Microcontroller The ESP32 integrated with Antenna switches, RF Balun, power amplifiers, low-noise amplifiers, filters, and management modules, and the entire solution occupies the least area of PCB. 2.4 GHz Wi-Fi plus Bluetooth dual-mode chip, with TSMC Ultra-low power consumption 40nm technology,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
  ESP32 - CAM: The ESP32-CAM has a very competitive small-size camera module that can operate independently as a minimum system with a footprint of only 27*40.5*4.5mm and a deep sleep current of up to 6mA.
